// Logisim project 4DigitDisplay.circ as structural Verilog: 2 circuits, main circuit main
module main (
  input  in_1,
  output [3:0] out_2,
  output [3:0] out_3,
  output [3:0] out_4
);

  wire a1, a2, a3, a4, b1, b2, b3, b4, c1, c2, c3, c4, clock_1_out, clock_2_out, clock_3_out, clock_4_out,
       clock_5_out, d1, d2, d3, d4, e1, e2, e3, e4, f1, f2, f3, f4, g1, g2, g3, g4;
  wire [3:0] Data_In, register_1_q, register_2_q, register_3_q, register_4_q;

  Clock clock_1 (.out(clock_1_out));
  Counter #(.width(4), .max('h9)) counter_1 (
    .Q(Data_In), .clk(clock_1_out), .clr(in_1));  // open: load, D, count, carry
  Counter #(.width(4), .max('h9)) counter_2 (.Q(out_2), .clk(clock_1_out), .clr(in_1));  // open: load, D, count, carry
  Counter #(.width(4), .max('h9)) counter_3 (.Q(out_3), .clk(clock_1_out), .clr(in_1));  // open: load, D, count, carry
  Counter #(.width(4), .max('h9)) counter_4 (.Q(out_4), .clk(clock_1_out), .clr(in_1));  // open: load, D, count, carry
  Clock clock_2 (.out(clock_2_out));
  Clock #(.highDuration(2), .lowDuration(2)) clock_3 (.out(clock_3_out));
  Clock #(.highDuration(3), .lowDuration(3)) clock_4 (.out(clock_4_out));
  Clock #(.highDuration(4), .lowDuration(4)) clock_5 (.out(clock_5_out));
  Register #(.width(4)) register_1 (.D(Data_In), .Q(register_1_q), .clk(clock_2_out));  // open: en, clr
  Register #(.width(4)) register_2 (.D(out_2), .Q(register_2_q), .clk(clock_3_out));  // open: en, clr
  Register #(.width(4)) register_3 (.D(out_3), .Q(register_3_q), .clk(clock_4_out));  // open: en, clr
  Register #(.width(4)) register_4 (.D(out_4), .Q(register_4_q), .clk(clock_5_out));  // open: en, clr
  BCD_decoder bcd_decoder_1 (
    .B3(register_1_q[3]), .B2(register_1_q[2]), .B1(register_1_q[1]), .B0(register_1_q[0]), .a(a1), .b(b1),
    .c(c1), .d(d1), .e(e1), .f(f1), .g(g1));
  BCD_decoder bcd_decoder_2 (
    .B3(register_2_q[3]), .B2(register_2_q[2]), .B1(register_2_q[1]), .B0(register_2_q[0]), .a(a2), .b(b2),
    .c(c2), .d(d2), .e(e2), .f(f2), .g(g2));
  BCD_decoder bcd_decoder_3 (
    .B3(register_3_q[3]), .B2(register_3_q[2]), .B1(register_3_q[1]), .B0(register_3_q[0]), .a(a3), .b(b3),
    .c(c3), .d(d3), .e(e3), .f(f3), .g(g3));
  BCD_decoder bcd_decoder_4 (
    .B3(register_4_q[3]), .B2(register_4_q[2]), .B1(register_4_q[1]), .B0(register_4_q[0]), .a(a4), .b(b4),
    .c(c4), .d(d4), .e(e4), .f(f4), .g(g4));
  _7_Segment_Display u_7_segment_display_1 (.g(g4), .f(f4), .a(a4), .b(b4), .e(e4), .d(d4), .c(c4));  // open: dp
  _7_Segment_Display u_7_segment_display_2 (.g(g3), .f(f3), .a(a3), .b(b3), .e(e3), .d(d3), .c(c3));  // open: dp
  _7_Segment_Display u_7_segment_display_3 (.g(g2), .f(f2), .a(a2), .b(b2), .e(e2), .d(d2), .c(c2));  // open: dp
  _7_Segment_Display u_7_segment_display_4 (.g(g1), .f(f1), .a(a1), .b(b1), .e(e1), .d(d1), .c(c1));  // open: dp

  // Other names for the same wires on the sheet: Data_In[15:4] = {out_4, out_3, out_2}

  // Notes on the sheet:
  //   Auto Test Counter CKTs:
  //   Reset Counters
endmodule

module BCD_decoder (
  input  B3,
  input  B2,
  input  B1,
  input  B0,
  output a,
  output b,
  output c,
  output d,
  output e,
  output f,
  output g
);

  wire and_1_out, B1_nB0_out, B1B0_out, B2_nB0_out, B2_nB1_out, B2B0_nB1_out, B2B0_out, nB0, nB1,
       nB1_nB0_out, nB2, nB2_nB0_out, nB2B1_out, nB3, nB_0_3_out;

  and nB2_nB0 (nB2_nB0_out, nB2, nB0);
  and B2B0 (B2B0_out, B2, B0);
  and nB_0_3 (nB_0_3_out, nB3, nB2, nB1, nB0);
  and B1B0 (B1B0_out, B1, B0);
  and nB1_nB0 (nB1_nB0_out, nB1, nB0);
  and B2B0_nB1 (B2B0_nB1_out, B2, B0, nB1);
  and nB2B1 (nB2B1_out, nB2, B1);
  and B2_nB0 (B2_nB0_out, B2, nB0);
  and B2_nB1 (B2_nB1_out, B2, nB1);
  and B1_nB0 (B1_nB0_out, B1, nB0);
  or or_1 (a, B3, nB2_nB0_out, B2B0_out, B1);
  or or_2 (b, B3, nB2, nB1_nB0_out, B1B0_out);
  or or_3 (c, B2, nB1_nB0_out, B0);
  or or_4 (d, B3, nB2_nB0_out, B1_nB0_out, B2B0_nB1_out, nB2B1_out);
  or or_5 (f, B3, nB1_nB0_out, B2_nB0_out, B2_nB1_out);
  or or_6 (g, B3, B1_nB0_out, nB2B1_out, B2_nB1_out);
  not not_1 (nB0, B0);
  not not_2 (nB1, B1);
  and and_1 (and_1_out, nB0, B3);
  not not_3 (nB3, B3);
  not not_4 (nB2, B2);
  or or_7 (e, and_1_out, nB_0_3_out, B1_nB0_out);

  // Notes on the sheet:
  //   B3: pull=down
  //   B1: pull=down
  //   B0: pull=down
  //   B2: pull=down
  //   BCD Decoder
endmodule
