// Logisim project 7Seg-simple.circ as structural Verilog: 1 circuit, main circuit main
module main (
  input  B3,
  input  B2,
  input  B1,
  input  B0,
  output [4:0] out_5,
  output [3:0] out_6
);

  wire a, and_1_out, b, B1_nB0_out, B1B0_out, B2_nB0_out, B2_nB1_out, B2B0_nB1_out, B2B0_out, c, d, e, f, g,
       I, nB0, nB1, nB1_nB0_out, nB2, nB2_nB0_out, nB2B1_out, nB3, nB_0_3_out;

  and nB2_nB0 (nB2_nB0_out, nB2, nB0);
  and B2B0 (B2B0_out, out_6[2], out_6[0]);
  and nB_0_3 (nB_0_3_out, nB3, nB2, nB1, nB0);
  and B1B0 (B1B0_out, out_6[1], out_6[0]);
  and nB1_nB0 (nB1_nB0_out, nB1, nB0);
  and B2B0_nB1 (B2B0_nB1_out, out_6[2], out_6[0], nB1);
  and nB2B1 (nB2B1_out, nB2, out_6[1]);
  and B2_nB0 (B2_nB0_out, out_6[2], nB0);
  and B2_nB1 (B2_nB1_out, out_6[2], nB1);
  and B1_nB0 (B1_nB0_out, out_6[1], nB0);
  not not_1 (I, out_5[4]);
  or or_1 (a, out_6[3], nB2_nB0_out, B2B0_out, out_6[1]);
  or or_2 (b, out_6[3], nB2, nB1_nB0_out, B1B0_out);
  or or_3 (c, out_6[2], nB1_nB0_out, out_6[0]);
  or or_4 (d, out_6[3], nB2_nB0_out, B1_nB0_out, B2B0_nB1_out, nB2B1_out);
  or or_5 (f, out_6[3], nB1_nB0_out, B2_nB0_out, B2_nB1_out);
  or or_6 (g, out_6[3], B1_nB0_out, nB2B1_out, B2_nB1_out);
  _4bitSubtractor u_4bitsubtractor_1 (.X({B3, B2, B1, B0}), .Y(4'b1010), .Output(out_5));
  Multiplexer #(.width(4), .enable("false")) multiplexer_1 (
    .in0(out_5[3:0]), .in1({B3, B2, B1, B0}), .out(out_6), .sel(out_5[4]));
  and and_1 (and_1_out, nB0, out_6[3]);
  not not_2 (nB1, out_6[1]);
  not not_3 (nB2, out_6[2]);
  not not_4 (nB0, out_6[0]);
  or or_7 (e, and_1_out, nB_0_3_out, B1_nB0_out);
  not not_5 (nB3, out_6[3]);
  _7_Segment_Display u_7_segment_display_1 (.b(I), .c(I));  // open: g, f, a, e, d, dp
  _7_Segment_Display u_7_segment_display_2 (.g(g), .f(f), .a(a), .b(b), .e(e), .d(d), .c(c));  // open: dp

  // Other names for the same wires on the sheet: p0 = B0; p1 = B1; p2 = B2; p3 = B3; B0_t = out_6[0]; B1_t = out_6[1];
  //   B2_t = out_6[2]; B3_t = out_6[3]

  // Notes on the sheet:
  //   B1: pull=down
  //   B2: pull=down
  //   B0: pull=down
  //   B3: pull=down
  //   Manual Test:
  //   Input Bits
  //   BCD Decoder
  //   Carry 1 Display Ctrl
  //   Subtractor: Subtracts 10 from any given 4 Bit Value
  //   Hardcoded 10
  //   Current MUX Output
  //   The SIGN bit (first bit) will be used to control the Bit MUX
  //   These Signals are actually fed to the BCD Decoder
  //   A
  //   H
  //   after we subtract 10 and use the carry bit to select the right signal from the MUX.
  //   Business end of things: The Display (output)
  //   Display is labeled using standard BCD 7-Segment Code [a-g]
endmodule
