// Logisim project 7Seg.circ as structural Verilog: 1 circuit, main circuit main
module main (
  input  B3,
  input  B2,
  input  B1,
  input  B0,
  input  Auto,
  output [3:0] out_6,
  output [4:0] out_7,
  output [3:0] out_8
);

  wire a, and_1_out, b, B1_nB0_out, B1B0_out, B2_nB0_out, B2_nB1_out, B2B0_nB1_out, B2B0_out, c, clock_1_out,
       d, e, f, g, I, nB0, nB1, nB1_nB0_out, nB2, nB2_nB0_out, nB2B1_out, nB3, nB_0_3_out, not_6_out, p0, p1,
       p2, p3;

  and nB2_nB0 (nB2_nB0_out, nB2, nB0);
  and B2B0 (B2B0_out, out_8[2], out_8[0]);
  and nB_0_3 (nB_0_3_out, nB3, nB2, nB1, nB0);
  and B1B0 (B1B0_out, out_8[1], out_8[0]);
  and nB1_nB0 (nB1_nB0_out, nB1, nB0);
  and B2B0_nB1 (B2B0_nB1_out, out_8[2], out_8[0], nB1);
  and nB2B1 (nB2B1_out, nB2, out_8[1]);
  and B2_nB0 (B2_nB0_out, out_8[2], nB0);
  and B2_nB1 (B2_nB1_out, out_8[2], nB1);
  and B1_nB0 (B1_nB0_out, out_8[1], nB0);
  not not_1 (I, out_7[4]);
  or or_1 (a, out_8[3], nB2_nB0_out, B2B0_out, out_8[1]);
  or or_2 (b, out_8[3], nB2, nB1_nB0_out, B1B0_out);
  or or_3 (c, out_8[2], nB1_nB0_out, out_8[0]);
  or or_4 (d, out_8[3], nB2_nB0_out, B1_nB0_out, B2B0_nB1_out, nB2B1_out);
  or or_5 (f, out_8[3], nB1_nB0_out, B2_nB0_out, B2_nB1_out);
  or or_6 (g, out_8[3], B1_nB0_out, nB2B1_out, B2_nB1_out);
  _4bitSubtractor u_4bitsubtractor_1 (.X({p3, p2, p1, p0}), .Y(4'b1010), .Output(out_7));
  Multiplexer #(.width(4), .enable("false")) multiplexer_1 (
    .in0(out_7[3:0]), .in1({p3, p2, p1, p0}), .out(out_8), .sel(out_7[4]));
  and and_1 (and_1_out, nB0, out_8[3]);
  not not_2 (nB1, out_8[1]);
  not not_3 (nB2, out_8[2]);
  not not_4 (nB0, out_8[0]);
  or or_7 (e, and_1_out, nB_0_3_out, B1_nB0_out);
  not not_5 (nB3, out_8[3]);
  _7_Segment_Display u_7_segment_display_1 (.b(I), .c(I));  // open: g, f, a, e, d, dp
  _7_Segment_Display u_7_segment_display_2 (.g(g), .f(f), .a(a), .b(b), .e(e), .d(d), .c(c));  // open: dp
  Counter #(.width(4), .max('hf)) counter_1 (.Q(out_6), .clk(clock_1_out));  // open: load, D, count, carry, clr
  Clock clock_1 (.out(clock_1_out));
  not not_6 (not_6_out, Auto);
  Multiplexer #(.width(4), .enable("false")) multiplexer_2 (
    .in0(out_6), .in1({B3, B2, B1, B0}), .out({p3, p2, p1, p0}), .sel(not_6_out));

  // Other names for the same wires on the sheet: p0a = B0; p1a = B1; p2a = B2; p3a = B3; B0_t = out_8[0];
  //   B1_t = out_8[1]; B2_t = out_8[2]; B3_t = out_8[3]

  // Notes on the sheet:
  //   B0: pull=down
  //   B1: pull=down
  //   Auto: pull=down
  //   B3: pull=down
  //   B2: pull=down
  //   Manual Test:
  //   Input Bits
  //   Enable Auto Test:
  //   (note: also enable ticks!)
  //   BCD Decoder
  //   Carry 1 Display Ctrl
  //   Subtractor: Subtracts 10 from any given 4 Bit Value
  //   Hardcoded 10
  //   Current MUX Output
  //   The SIGN bit (first bit) will be used to control the Bit MUX
  //   These Signals are actually fed to the BCD Decoder
  //   A
  //   H
  //   after we subtract 10 and use the carry bit to select the right signal from the MUX.
  //   Auto Test Counter CKT:
  //   Business end of things: The Display (output)
  //   Display is labeled using standard BCD 7-Segment Code [a-g]
  //   Enable Ticks with Ctrl+K to Test.
  //   after enabling AUTO bit in 'Manual Test'
endmodule
