// Logisim project 7SegV2.circ as structural Verilog: 15 circuits, main circuit HalfAdder
module HalfAdder (
  input  X_0,
  input  X_1,
  output C__Carry_Out,
  output S__Sum
);

  and and_1 (C__Carry_Out, X_0, X_1);
  xor xor_1 (S__Sum, X_0, X_1);
endmodule

module FullAdder (
  input  X_0,
  input  X_1,
  input  C_in,
  output C_out,
  output S
);

  wire and_1_out, and_2_out, xor_1_out;

  and and_1 (and_1_out, X_0, X_1);
  xor xor_1 (xor_1_out, X_0, X_1);
  and and_2 (and_2_out, xor_1_out, C_in);
  or or_1 (C_out, and_1_out, and_2_out);
  xor xor_2 (S, xor_1_out, C_in);
endmodule

module AbstractedAdder (
  input  C_in,
  input  X_0,
  input  X_1,
  output S,
  output C_out
);

  Adder #(.width(1)) adder_1 (.a(X_0), .b(X_1), .out(S), .cin(C_in), .cout(C_out));
endmodule

module _2bitAdder (
  input  X_1,
  input  X_0,
  input  Y_1,
  input  Y_0,
  output S_0,
  output S_1,
  output Carry_Out
);

  wire adder_1_cout;

  Adder #(.width(1)) adder_1 (.a(Y_0), .b(X_0), .out(S_0), .cin(1'b0), .cout(adder_1_cout));
  Adder #(.width(1)) adder_2 (.a(Y_1), .b(X_1), .out(S_1), .cin(adder_1_cout), .cout(Carry_Out));
endmodule

module _3bitAdder (
  input  X_2,
  input  X_1,
  input  X_0,
  input  Y_2,
  input  Y_1,
  input  Y_0,
  output S_0,
  output S_1,
  output S_2,
  output Carry_Out
);

  wire adder_1_cout, adder_2_cout;

  Adder #(.width(1)) adder_1 (.a(Y_0), .b(X_0), .out(S_0), .cin(1'b0), .cout(adder_1_cout));
  Adder #(.width(1)) adder_2 (.a(Y_1), .b(X_1), .out(S_1), .cin(adder_1_cout), .cout(adder_2_cout));
  Adder #(.width(1)) adder_3 (.a(Y_2), .b(X_2), .out(S_2), .cin(adder_2_cout), .cout(Carry_Out));
endmodule

module _4bitAdder (
  input  [3:0] X,
  input  [3:0] Y,
  output [4:0] Output
);

  wire adder_1_cout, adder_2_cout, adder_3_cout;

  Adder #(.width(1)) adder_1 (.a(Y[0]), .b(X[0]), .out(Output[0]), .cin(1'b0), .cout(adder_1_cout));
  Adder #(.width(1)) adder_2 (.a(Y[1]), .b(X[1]), .out(Output[1]), .cin(adder_1_cout), .cout(adder_2_cout));
  Adder #(.width(1)) adder_3 (.a(Y[2]), .b(X[2]), .out(Output[2]), .cin(adder_2_cout), .cout(adder_3_cout));
  Adder #(.width(1)) adder_4 (.a(Y[3]), .b(X[3]), .out(Output[3]), .cin(adder_3_cout), .cout(Output[4]));
endmodule

module HalfSubtractor (
  input  X_0,
  input  X_1,
  output B,
  output D
);

  wire not_1_out;

  not not_1 (not_1_out, X_0);
  and and_1 (B, not_1_out, X_1);
  xor xor_1 (D, X_0, X_1);
endmodule

module FullSubtractor (
  input  X_0,
  input  X_1,
  input  B_in,
  output B_out,
  output D
);

  wire and_1_out, and_2_out, and_3_out, not_1_out;

  not not_1 (not_1_out, B_in);
  and and_1 (and_1_out, X_0, not_1_out);
  and and_2 (and_2_out, X_0, X_1);
  and and_3 (and_3_out, X_1, not_1_out);
  or or_1 (B_out, and_1_out, and_2_out, and_3_out);
  ExactlyOne xor_1 (.out(D), .in0(X_0), .in1(X_1), .in2(B_in));
endmodule

module AbstractedSubtractor (
  input  B_in,
  input  X_0,
  input  X_1,
  output D,
  output B_out
);

  Subtractor #(.width(1)) subtractor_1 (.a(X_0), .b(X_1), .out(D), .bin(B_in), .bout(B_out));
endmodule

module _2bitSubtractor (
  input  [1:0] X,
  input  [1:0] Y,
  output [2:0] Output
);

  wire subtractor_1_bout;

  Subtractor #(.width(1)) subtractor_1 (.a(X[0]), .b(Y[0]), .out(Output[0]), .bout(subtractor_1_bout));  // open: bin
  Subtractor #(.width(1)) subtractor_2 (.a(X[1]), .b(Y[1]), .out(Output[1]), .bin(subtractor_1_bout), .bout(Output[2]));
endmodule

module _3bitSubtractor (
  input  [2:0] X,
  input  [2:0] Y,
  output [3:0] Output
);

  wire subtractor_1_bout, subtractor_2_bout;

  Subtractor #(.width(1)) subtractor_1 (.a(X[0]), .b(Y[0]), .out(Output[0]), .bout(subtractor_1_bout));  // open: bin
  Subtractor #(.width(1)) subtractor_2 (
    .a(X[1]), .b(Y[1]), .out(Output[1]), .bin(subtractor_1_bout), .bout(subtractor_2_bout));
  Subtractor #(.width(1)) subtractor_3 (.a(X[2]), .b(Y[2]), .out(Output[2]), .bin(subtractor_2_bout), .bout(Output[3]));
endmodule

module _4bitSubtractor (
  input  [3:0] X,
  input  [3:0] Y,
  output [4:0] Output
);

  wire subtractor_1_bout, subtractor_2_bout, subtractor_3_bout;

  Subtractor #(.width(1)) subtractor_1 (.a(X[0]), .b(Y[0]), .out(Output[0]), .bout(subtractor_1_bout));  // open: bin
  Subtractor #(.width(1)) subtractor_2 (
    .a(X[1]), .b(Y[1]), .out(Output[1]), .bin(subtractor_1_bout), .bout(subtractor_2_bout));
  Subtractor #(.width(1)) subtractor_3 (
    .a(X[2]), .b(Y[2]), .out(Output[2]), .bin(subtractor_2_bout), .bout(subtractor_3_bout));
  Subtractor #(.width(1)) subtractor_4 (.a(X[3]), .b(Y[3]), .out(Output[3]), .bin(subtractor_3_bout), .bout(Output[4]));
endmodule

module _2bitMultiplier (
  input  X_1,
  input  X_0,
  input  Y_0,
  input  Y_1,
  output P_0,
  output P_1,
  output P_2,
  output P_3
);

  wire adder_1_cout, and_1_out, and_2_out, and_4_out;

  and and_1 (and_1_out, Y_1, X_1);
  and and_2 (and_2_out, Y_1, X_0);
  and and_3 (P_0, Y_0, X_0);
  and and_4 (and_4_out, Y_0, X_1);
  Adder #(.width(1)) adder_1 (.a(and_4_out), .b(and_2_out), .out(P_1), .cout(adder_1_cout));  // open: cin
  Adder #(.width(1)) adder_2 (.a(adder_1_cout), .b(and_1_out), .out(P_2), .cout(P_3));  // open: cin
endmodule

module _3bitMultiplier (
  input  X_2,
  input  X_1,
  input  X_0,
  input  Y_0,
  input  Y_1,
  input  Y_2,
  output P_0,
  output P_1,
  output P_2,
  output P_3,
  output P_4,
  output P_5
);

  wire adder_1_cout, adder_2_cout, adder_2_out, adder_3_cout, adder_3_out, adder_4_cout, adder_5_cout,
       and_1_out, and_2_out, and_3_out, and_4_out, and_5_out, and_6_out, and_7_out, and_8_out;

  and and_1 (and_1_out, Y_2, X_2);
  and and_2 (and_2_out, Y_2, X_1);
  and and_3 (and_3_out, Y_2, X_0);
  and and_4 (and_4_out, Y_1, X_2);
  and and_5 (and_5_out, Y_1, X_1);
  and and_6 (and_6_out, Y_0, X_2);
  and and_7 (and_7_out, Y_1, X_0);
  and and_8 (and_8_out, Y_0, X_1);
  and and_9 (P_0, Y_0, X_0);
  Adder #(.width(1)) adder_1 (.a(and_8_out), .b(and_7_out), .out(P_1), .cout(adder_1_cout));  // open: cin
  Adder #(.width(1)) adder_2 (.a(and_6_out), .b(and_5_out), .out(adder_2_out), .cout(adder_2_cout));  // open: cin
  Adder #(.width(1)) adder_3 (.a(and_4_out), .b(and_2_out), .out(adder_3_out), .cin(adder_2_cout), .cout(adder_3_cout));
  Adder #(.width(1)) adder_4 (.a(adder_2_out), .b(and_3_out), .out(P_2), .cin(adder_1_cout), .cout(adder_4_cout));
  Adder #(.width(1)) adder_5 (.a(adder_4_cout), .b(adder_3_out), .out(P_3), .cout(adder_5_cout));  // open: cin
  Adder #(.width(1)) adder_6 (.a(adder_3_cout), .b(and_1_out), .out(P_4), .cin(adder_5_cout), .cout(P_5));
endmodule

module SevenSegment (
  input  B3,
  input  B2,
  input  B1,
  input  B0
);

  wire n2bitadder_1_carry_out, n2bitadder_1_s_0, n2bitadder_1_s_1, nB0, nB1, nB2, nB3;

  not not_1 (nB2, B2);
  not not_2 (nB3, B3);
  not not_3 (nB0, B0);
  not not_4 (nB1, B1);
  _2bitAdder u_2bitadder_1 (
    .X_1(B0), .X_0(B1), .Y_1(B2), .Y_0(B3), .S_0(n2bitadder_1_s_0), .S_1(n2bitadder_1_s_1),
    .Carry_Out(n2bitadder_1_carry_out));
  LED led_1 (.in(n2bitadder_1_s_0));
  LED led_2 (.in(n2bitadder_1_s_1));
  LED led_3 (.in(n2bitadder_1_carry_out));
  _2bitAdder u_2bitadder_2 ();  // open: X_1, X_0, Y_1, Y_0, S_0, S_1, Carry_Out

  // Notes on the sheet:
  //   B1: pull=down
  //   B2: pull=down
  //   B3: pull=down
  //   B0: pull=down
endmodule
