// Logisim project Gray Code Encoder-Decoder.circ as structural Verilog: 1 circuit, main circuit main
module main (
  input  B3,
  input  B2,
  input  B1,
  input  B0,
  output G3,
  output B_prime_3,
  output B_prime_2,
  output G2,
  output B_prime_1,
  output G1,
  output B_prime_0,
  output G0
);

  xor xor_1 (G2, B3, B2);
  xor xor_2 (G1, B2, B1);
  xor xor_3 (G0, B1, B0);
  xor xor_4 (B_prime_2, B3, G2);
  xor xor_5 (B_prime_1, B_prime_2, G1);
  xor xor_6 (B_prime_0, B_prime_1, G0);

  assign B_prime_3 = B3;
  assign G3 = B3;

  // Notes on the sheet:
  //   B0: pull=down
  //   B3: pull=down
  //   B2: pull=down
  //   B1: pull=down
  //   Input Bits
  //   Binary Input
  //   Gray Code Encoder Circuit
  //   Output Bits
  //   Gray Code Decoder Circuit
  //   Gray code to Binary Bits Output
endmodule
