// Logisim project Module6.circ as structural Verilog: 11 circuits, main circuit Gates
module Bus1 (
  input  [15:0] _16_bit_Bus,
  output [3:0] _4_bit_Bus,
  output [3:0] _4_bit_Bus_2,
  output [3:0] _4_bit_Bus_3,
  output [3:0] _4_bit_Bus_4
);


  assign _4_bit_Bus = _16_bit_Bus[3:0];
  assign _4_bit_Bus_2 = _16_bit_Bus[7:4];
  assign _4_bit_Bus_3 = _16_bit_Bus[11:8];
  assign _4_bit_Bus_4 = _16_bit_Bus[15:12];

  // Notes on the sheet:
  //   Split to two 8-bit busses
  //   Split to two 4-bit busses
  //   Split to two 4-bit busses
endmodule

module Bus2 (
  input  [3:0] _4_bit_Bus,
  input  [3:0] _4_bit_Bus_2,
  input  [3:0] _4_bit_Bus_3,
  input  [3:0] _4_bit_Bus_4,
  output [15:0] out_5
);


  assign out_5 = {_4_bit_Bus_4, _4_bit_Bus_3, _4_bit_Bus_2, _4_bit_Bus};

  // Notes on the sheet:
  //   Bundle to one 8-bit bus
  //   Bundle to one 8-bit bus
  //   Bundle to one 16-bit bus
endmodule

module Bus3 (
  input  [3:0] _4_bit_Bus,
  input  [3:0] _4_bit_Bus_2,
  input  [3:0] _4_bit_Bus_3,
  input  [3:0] _4_bit_Bus_4,
  output [15:0] out_5
);


  assign out_5 = {_4_bit_Bus_4, _4_bit_Bus_3, _4_bit_Bus_2, _4_bit_Bus};

  // Notes on the sheet:
  //   Bundle to one 16-bit bus
endmodule

module Gates (
  input  x,
  input  x_2,
  input  y,
  input  y_2,
  input  x_3,
  input  x_4,
  input  y_3,
  input  y_4,
  input  x_5,
  input  NOT,
  input  y_5,
  input  x_6,
  input  y_6,
  output out_14,
  output out_15,
  output out_16,
  output out_17,
  output out_18,
  output out_19,
  output out_20
);

  and and_1 (out_14, x, x, y, y);
  or or_1 (out_16, x_3, x_3, y_3, y_3);
  not not_1 (out_18, NOT);
  nand nand_1 (out_20, x_6, x_6, y_6, y_6);
  ExactlyOne xor_1 (.out(out_15), .in0(x_2), .in1(x_2), .in3(y_2), .in4(y_2));
  nor nor_1 (out_19, x_5, x_5, y_5, y_5);
  NotExactlyOne xnor_1 (.out(out_17), .in0(x_4), .in1(x_4), .in3(y_4), .in4(y_4));

  // Notes on the sheet:
  //   AND
  //   OR
  //   NAND
  //   XOR
  //   XNOR
  //   NOR
endmodule

module Sample (
  input  x,
  input  y,
  input  z,
  output F
);

  wire not_1_out, or_1_out, xor_1_out;

  not not_1 (not_1_out, z);
  or or_1 (or_1_out, y, x);
  xor xor_1 (xor_1_out, z, y);
  and and_1 (F, not_1_out, xor_1_out, or_1_out);

  // Notes on the sheet:
  //   (x+y)(y xor z)(~z)
endmodule

module Practice1 (
);


  // Notes on the sheet:
  //   Create a logic circuit for: x + ~(xy)
endmodule

module Practice2 (
);


  // Notes on the sheet:
  //   Create a logic circuit for: (x+y)(x+z)
endmodule

module Practice3 (
);


  // Notes on the sheet:
  //   Create a logic circuit for: (~x)(~y)z + ~(xy+xz)
endmodule

module Practice4 (
);


  // Notes on the sheet:
  //   Create a logic circuit for: (x + y)(~x + y + ~z)
endmodule

module NANDonly (
  input  AND,
  input  XOR,
  input  in_3,
  input  in_4,
  input  XNOR,
  input  OR,
  input  in_7,
  input  in_8,
  input  NOR,
  input  NOT,
  input  in_11,
  output out_12,
  output out_13,
  output out_14,
  output out_15,
  output out_16,
  output out_17,
  output out_18,
  output out_19,
  output out_20,
  output out_21,
  output out_22,
  output out_23
);

  wire nand_1_out, nand_2_out, nand_3_out, nand_7_out, nand_8_out, nand_9_out, nand_10_out, nand_11_out,
       nand_12_out, nand_13_out, nand_14_out, nand_15_out, nand_16_out, undriven, undriven_2, undriven_3,
       undriven_4;

  and and_1 (out_12, AND, in_3);
  nand nand_1 (nand_1_out, AND, in_3);
  or or_1 (out_17, OR, in_8);
  nand nand_2 (nand_2_out, OR, OR, undriven);
  nand nand_3 (nand_3_out, undriven, in_8, in_8);
  not not_1 (out_20, NOT);
  nand nand_4 (out_22, NOT, NOT);
  nand nand_5 (out_15, nand_1_out, nand_1_out);
  nand nand_6 (out_19, nand_2_out, nand_3_out);
  xor xor_1 (out_13, XOR, in_4);
  nand nand_7 (nand_7_out, XOR, in_4);
  xnor xnor_1 (out_16, XNOR, in_7);
  nand nand_8 (nand_8_out, XNOR, XNOR, undriven_2);
  nand nand_9 (nand_9_out, undriven_2, in_7, in_7);
  nor nor_1 (out_21, NOR, in_11);
  nand nand_10 (nand_10_out, NOR, NOR, undriven_3);
  nand nand_11 (nand_11_out, undriven_3, in_11, in_11);
  nand nand_12 (nand_12_out, XOR, nand_7_out, undriven_4);
  nand nand_13 (nand_13_out, undriven_4, nand_7_out, in_4);
  nand nand_14 (nand_14_out, nand_8_out, nand_9_out);
  nand nand_15 (nand_15_out, XNOR, in_7);
  nand nand_16 (nand_16_out, nand_10_out, nand_11_out);
  nand nand_17 (out_14, nand_12_out, nand_13_out);
  nand nand_18 (out_18, nand_14_out, nand_15_out);
  nand nand_19 (out_23, nand_16_out, nand_16_out);
endmodule

module NORonly (
  input  AND,
  input  XOR,
  input  in_3,
  input  in_4,
  input  OR,
  input  in_6,
  input  XNOR,
  input  in_8,
  input  NOT,
  input  NAND,
  input  in_11,
  output out_12,
  output out_13,
  output out_14,
  output out_15,
  output out_16,
  output out_17,
  output out_18,
  output out_19,
  output out_20,
  output out_21,
  output out_22,
  output out_23
);

  wire nor_1_out, nor_2_out, nor_3_out, nor_7_out, nor_8_out, nor_9_out, nor_10_out, nor_11_out, nor_12_out,
       nor_13_out, nor_14_out, nor_15_out, nor_16_out, undriven, undriven_2, undriven_3, undriven_4;

  and and_1 (out_12, AND, in_3);
  nor nor_1 (nor_1_out, AND, AND, undriven);
  nor nor_2 (nor_2_out, undriven, in_3, in_3);
  or or_1 (out_16, OR, in_6);
  nor nor_3 (nor_3_out, OR, in_6);
  not not_1 (out_20, NOT);
  nor nor_4 (out_21, NOT, NOT);
  nor nor_5 (out_14, nor_1_out, nor_2_out);
  nor nor_6 (out_18, nor_3_out, nor_3_out);
  xor xor_1 (out_13, XOR, in_4);
  nor nor_7 (nor_7_out, XOR, XOR, undriven_2);
  nor nor_8 (nor_8_out, undriven_2, in_4, in_4);
  xnor xnor_1 (out_17, XNOR, in_8);
  nor nor_9 (nor_9_out, XNOR, in_8);
  nand nand_1 (out_22, NAND, in_11);
  nor nor_10 (nor_10_out, NAND, NAND, undriven_3);
  nor nor_11 (nor_11_out, undriven_3, in_11, in_11);
  nor nor_12 (nor_12_out, nor_7_out, nor_8_out);
  nor nor_13 (nor_13_out, XOR, in_4);
  nor nor_14 (nor_14_out, XNOR, nor_9_out, undriven_4);
  nor nor_15 (nor_15_out, undriven_4, nor_9_out, in_8);
  nor nor_16 (nor_16_out, nor_10_out, nor_11_out);
  nor nor_17 (out_15, nor_12_out, nor_13_out);
  nor nor_18 (out_19, nor_14_out, nor_15_out);
  nor nor_19 (out_23, nor_16_out, nor_16_out);
endmodule
