// Logisim project Module7.circ as structural Verilog: 18 circuits, main circuit SignExtend
module SignExtend (
  input  [7:0] in_1,
  output [15:0] out_2
);


  assign out_2 = {{9{in_1[7]}}, in_1[6:0]};

  // Notes on the sheet:
  //   Sign Extend
endmodule

module _2x1Encoder (
  input  I_0,
  input  I_1,
  output E_0
);

  wire not_1_out;

  not not_1 (not_1_out, I_0);
  and and_1 (E_0, not_1_out, I_1);

  // Notes on the sheet:
  //   2x1 Encoder
endmodule

module _4x2Encoder (
  input  I_3,
  input  I_2,
  input  I_1,
  input  I_0,
  output E_1,
  output E_0
);

  wire and_1_out, and_2_out, and_3_out, not_1_out, not_2_out, not_3_out, not_4_out;

  not not_1 (not_1_out, I_3);
  not not_2 (not_2_out, I_2);
  not not_3 (not_3_out, I_1);
  not not_4 (not_4_out, I_0);
  and and_1 (and_1_out, not_1_out, I_2, not_3_out, not_4_out);
  and and_2 (and_2_out, I_3, not_2_out, not_3_out, not_4_out);
  and and_3 (and_3_out, not_1_out, not_2_out, I_1, not_4_out);
  or or_1 (E_1, and_1_out, and_2_out);
  or or_2 (E_0, and_2_out, and_3_out);

  // Notes on the sheet:
  //   4x2 Encoder
endmodule

module _8x3Encoder (
  input  I_7,
  input  I_6,
  input  I_5,
  input  I_4,
  input  I_3,
  input  I_2,
  input  I_1,
  input  I_0,
  output E_2,
  output E_1,
  output E_0
);

  wire I_1_out, I_2_out, I_3_out, I_4_out, I_5_out, I_6_out, I_7_out, not_1_out, not_2_out, not_3_out,
       not_4_out, not_5_out, not_6_out, not_7_out, not_8_out;

  not not_1 (not_1_out, I_7);
  not not_2 (not_2_out, I_5);
  not not_3 (not_3_out, I_6);
  not not_4 (not_4_out, I_3);
  not not_5 (not_5_out, I_4);
  not not_6 (not_6_out, I_2);
  not not_7 (not_7_out, I_1);
  not not_8 (not_8_out, I_0);
  and u_I_4 (I_4_out, not_1_out, not_3_out, not_2_out, I_4, not_4_out, not_6_out, not_7_out, not_8_out);
  and u_I_5 (I_5_out, not_1_out, not_3_out, I_5, not_5_out, not_4_out, not_6_out, not_7_out, not_8_out);
  and u_I_6 (I_6_out, not_1_out, I_6, not_2_out, not_5_out, not_4_out, not_6_out, not_7_out, not_8_out);
  and u_I_3 (I_3_out, not_1_out, not_3_out, not_2_out, not_5_out, I_3, not_6_out, not_7_out, not_8_out);
  and u_I_7 (I_7_out, I_7, not_3_out, not_2_out, not_5_out, not_4_out, not_6_out, not_7_out, not_8_out);
  and u_I_2 (I_2_out, not_1_out, not_3_out, not_2_out, not_5_out, not_4_out, I_2, not_7_out, not_8_out);
  and u_I_1 (I_1_out, not_1_out, not_3_out, not_2_out, not_5_out, not_4_out, not_6_out, I_1, not_8_out);
  or or_1 (E_2, I_4_out, I_5_out, I_6_out, I_7_out);
  or or_2 (E_1, I_6_out, I_7_out, I_3_out, I_2_out);
  or or_3 (E_0, I_7_out, I_5_out, I_3_out, I_1_out);

  // Notes on the sheet:
  //   8x3 Encoder
endmodule

module _8x3EncoderWithBuses (
  input  [7:0] Inputs,
  output [2:0] Encoded_Ouput
);

  wire I_1_out, I_2_out, I_3_out, I_4_out, I_5_out, I_6_out, I_7_out, not_1_out, not_2_out, not_3_out,
       not_4_out, not_5_out, not_6_out, not_7_out, not_8_out;

  not not_1 (not_1_out, Inputs[7]);
  not not_2 (not_2_out, Inputs[5]);
  not not_3 (not_3_out, Inputs[6]);
  not not_4 (not_4_out, Inputs[3]);
  not not_5 (not_5_out, Inputs[4]);
  not not_6 (not_6_out, Inputs[1]);
  not not_7 (not_7_out, Inputs[2]);
  not not_8 (not_8_out, Inputs[0]);
  and I_4 (I_4_out, not_1_out, not_3_out, not_2_out, Inputs[4], not_4_out, not_7_out, not_6_out, not_8_out);
  and I_5 (I_5_out, not_1_out, not_3_out, Inputs[5], not_5_out, not_4_out, not_7_out, not_6_out, not_8_out);
  and I_6 (I_6_out, not_1_out, Inputs[6], not_2_out, not_5_out, not_4_out, not_7_out, not_6_out, not_8_out);
  and I_3 (I_3_out, not_1_out, not_3_out, not_2_out, not_5_out, Inputs[3], not_7_out, not_6_out, not_8_out);
  and I_7 (I_7_out, Inputs[7], not_3_out, not_2_out, not_5_out, not_4_out, not_7_out, not_6_out, not_8_out);
  and I_2 (I_2_out, not_1_out, not_3_out, not_2_out, not_5_out, not_4_out, Inputs[2], not_6_out, not_8_out);
  and I_1 (I_1_out, not_1_out, not_3_out, not_2_out, not_5_out, not_4_out, not_7_out, Inputs[1], not_8_out);
  or or_1 (Encoded_Ouput[2], I_4_out, I_5_out, I_6_out, I_7_out);
  or or_2 (Encoded_Ouput[1], I_6_out, I_7_out, I_3_out, I_2_out);
  or or_3 (Encoded_Ouput[0], I_7_out, I_5_out, I_3_out, I_1_out);

  // Notes on the sheet:
  //   8x3 Encoder with Buses
endmodule

module _1x2Decoder (
  input  I_0,
  output D_0,
  output D_1
);

  not not_1 (D_1, I_0);

  assign D_0 = I_0;

  // Notes on the sheet:
  //   1x2 Decoder
endmodule

module _2x4Decoder (
  input  I_0,
  input  I_1,
  output D_0,
  output D_1,
  output D_2,
  output D_3
);

  wire not_1_out, not_2_out, undriven, undriven_2, undriven_3;

  not not_1 (not_1_out, I_0);
  not not_2 (not_2_out, I_1);
  and and_1 (D_0, not_1_out, not_2_out, undriven);
  and and_2 (D_1, undriven, I_0, not_2_out, undriven_2);
  and and_3 (D_2, undriven_2, not_1_out, I_1, undriven_3);
  and and_4 (D_3, undriven_3, I_0, I_1);

  // Notes on the sheet:
  //   2x4 Decoder
endmodule

module _3x8Decoder (
  input  I_0,
  input  I_1,
  input  I_2,
  output D_0,
  output D_1,
  output D_2,
  output D_3,
  output D_4,
  output D_5,
  output D_6,
  output D_7
);

  wire not_1_out, not_2_out, not_3_out;

  not not_1 (not_1_out, I_0);
  not not_2 (not_2_out, I_1);
  not not_3 (not_3_out, I_2);
  and and_1 (D_0, not_1_out, not_2_out, not_3_out);
  and and_2 (D_1, I_0, not_2_out, not_3_out);
  and and_3 (D_2, not_1_out, I_1, not_3_out);
  and and_4 (D_3, I_0, I_1, not_3_out);
  and and_5 (D_4, not_1_out, not_2_out, I_2);
  and and_6 (D_5, I_0, not_2_out, I_2);
  and and_7 (D_6, not_1_out, I_1, I_2);
  and and_8 (D_7, I_0, I_1, I_2);

  // Notes on the sheet:
  //   3x8 Decoder
endmodule

module _3x8DecoderWithBuses (
  input  [2:0] Inputs,
  output [7:0] Decoded_Output
);

  wire not_1_out, not_2_out, not_3_out;

  not not_1 (not_1_out, Inputs[1]);
  not not_2 (not_2_out, Inputs[0]);
  not not_3 (not_3_out, Inputs[2]);
  and and_1 (Decoded_Output[0], not_2_out, not_1_out, not_3_out);
  and and_2 (Decoded_Output[1], Inputs[0], not_1_out, not_3_out);
  and and_3 (Decoded_Output[2], not_2_out, Inputs[1], not_3_out);
  and and_4 (Decoded_Output[3], Inputs[0], Inputs[1], not_3_out);
  and and_5 (Decoded_Output[4], not_2_out, not_1_out, Inputs[2]);
  and and_6 (Decoded_Output[5], Inputs[0], not_1_out, Inputs[2]);
  and and_7 (Decoded_Output[6], not_2_out, Inputs[1], Inputs[2]);
  and and_8 (Decoded_Output[7], Inputs[0], Inputs[1], Inputs[2]);

  // Notes on the sheet:
  //   3x8 Decoder with Buses
endmodule

module _4x1Multiplexer (
  input  I_0,
  input  I_1,
  input  I_2,
  input  I_3,
  input  S_1,
  input  S_0,
  output out_7
);

  wire and_1_out, and_2_out, and_3_out, and_4_out, not_1_out, not_2_out;

  not not_1 (not_1_out, S_1);
  not not_2 (not_2_out, S_0);
  and and_1 (and_1_out, I_0, not_1_out, not_2_out);
  and and_2 (and_2_out, I_1, not_1_out, S_0);
  and and_3 (and_3_out, I_2, S_1, not_2_out);
  and and_4 (and_4_out, I_3, S_1, S_0);
  or or_1 (out_7, and_1_out, and_2_out, and_3_out, and_4_out);

  // Notes on the sheet:
  //   4x1 Multiplexer
endmodule

module _8x1Multiplexer (
  input  I_0,
  input  I_1,
  input  I_2,
  input  I_3,
  input  I_4,
  input  I_5,
  input  I_6,
  input  I_7,
  input  S_2,
  input  S_1,
  input  S_0,
  output out_12
);

  wire and_1_out, and_2_out, and_3_out, and_4_out, and_5_out, and_6_out, and_7_out, and_8_out, not_1_out,
       not_2_out, not_3_out;

  not not_1 (not_1_out, S_2);
  not not_2 (not_2_out, S_1);
  not not_3 (not_3_out, S_0);
  and and_1 (and_1_out, I_0, not_1_out, not_2_out, not_3_out);
  and and_2 (and_2_out, I_1, not_1_out, not_2_out, S_0);
  and and_3 (and_3_out, I_2, not_1_out, S_1, not_3_out);
  and and_4 (and_4_out, I_3, not_1_out, S_1, S_0);
  and and_5 (and_5_out, I_4, S_2, not_2_out, not_3_out);
  and and_6 (and_6_out, I_5, S_2, not_2_out, S_0);
  and and_7 (and_7_out, I_6, S_2, S_1, not_3_out);
  and and_8 (and_8_out, I_7, S_2, S_1, S_0);
  or or_1 (out_12, and_1_out, and_2_out, and_3_out, and_4_out, and_5_out, and_6_out, and_7_out, and_8_out);
endmodule

module AbstractedMultiplexers (
  input  I_0,
  input  [3:0] I_0_2,
  input  I_0_3,
  input  I_1,
  input  I_1_2,
  input  [3:0] I_1_3,
  input  I_2,
  input  I_3,
  input  I_2_2,
  input  [3:0] I_2_3,
  input  I_4,
  input  I_3_2,
  input  [3:0] I_3_3,
  input  I_5,
  input  I_6,
  input  S_1,
  input  S_0,
  input  S_1_2,
  input  S_0_2,
  input  I_7,
  input  S_2,
  input  S_1_3,
  input  S_0_3,
  output out_24,
  output [3:0] out_25,
  output out_26
);

  Multiplexer #(.select(2)) multiplexer_1 (
    .in0(I_0), .in1(I_1_2), .in2(I_2_2), .in3(I_3_2), .out(out_24), .sel({S_1, S_0}));  // open: en
  Multiplexer #(.select(2), .width(4)) multiplexer_2 (
    .in0(I_0_2), .in1(I_1_3), .in2(I_2_3), .in3(I_3_3), .out(out_25), .sel({S_1_2, S_0_2}));  // open: en
  Multiplexer #(.select(3)) multiplexer_3 (
    .in0(I_0_3), .in1(I_1), .in2(I_2), .in3(I_3), .in4(I_4), .in5(I_5), .in6(I_6), .in7(I_7), .out(out_26),
    .sel({S_2, S_1_3, S_0_3}));  // open: en

  // Notes on the sheet:
  //   Abstracted 4x1 MUX
  //   Abstracted 4x1 MUX with Buses
  //   Abstracted 8x1 MUX
endmodule

module _8x16Multiplexer (
  input  [15:0] I_0,
  input  [15:0] I_1,
  input  [15:0] I_2,
  input  [15:0] I_3,
  input  [15:0] I_4,
  input  [15:0] I_5,
  input  S_2,
  input  S_1,
  input  S_0,
  input  [15:0] I_6,
  input  [15:0] I_7,
  output [15:0] out_12
);

  Multiplexer #(.select(3), .width(16)) multiplexer_1 (
    .in0(I_0), .in1(I_1), .in2(I_2), .in3(I_3), .in4(I_4), .in5(I_5), .in6(I_6), .in7(I_7), .out(out_12),
    .sel({S_2, S_1, S_0}));  // open: en

  // Notes on the sheet:
  //   Abstracted 8x16 MUX with Buses
endmodule

module _1x4Demultiplexer (
  input  I,
  input  S_1,
  input  S_0,
  output D_0,
  output D_1,
  output D_2,
  output D_3
);

  wire not_1_out, not_2_out;

  not not_1 (not_1_out, S_1);
  not not_2 (not_2_out, S_0);
  and and_1 (D_0, I, not_1_out, not_2_out);
  and and_2 (D_1, I, not_1_out, S_0);
  and and_3 (D_2, I, S_1, not_2_out);
  and and_4 (D_3, I, S_1, S_0);

  // Notes on the sheet:
  //   1x4 Demultiplexer
endmodule

module _1x8Demultiplexer (
  input  I,
  input  S_2,
  input  S_1,
  input  S_0,
  output D_0,
  output D_1,
  output D_2,
  output D_3,
  output D_4,
  output D_5,
  output D_6,
  output D_7
);

  wire not_1_out, not_2_out, not_3_out;

  not not_1 (not_1_out, S_2);
  not not_2 (not_2_out, S_0);
  not not_3 (not_3_out, S_1);
  and and_1 (D_0, I, not_1_out, not_3_out, not_2_out);
  and and_2 (D_1, I, not_1_out, not_3_out, S_0);
  and and_3 (D_2, I, not_1_out, S_1, not_2_out);
  and and_4 (D_3, I, not_1_out, S_1, S_0);
  and and_5 (D_4, I, S_2, not_3_out, not_2_out);
  and and_6 (D_5, I, S_2, not_3_out, S_0);
  and and_7 (D_6, I, S_2, S_1, not_2_out);
  and and_8 (D_7, I, S_2, S_1, S_0);

  // Notes on the sheet:
  //   1x8 Demultiplexer
endmodule

module AbstractedDemultiplexers (
  input  in_1,
  input  in_2,
  input  S_1,
  input  S_0,
  input  S_2,
  input  S_1_2,
  input  S_0_2,
  output D_0,
  output D_0_2,
  output D_1,
  output D_1_2,
  output D_2,
  output D_2_2,
  output D_3,
  output D_3_2,
  output D_4,
  output D_5,
  output D_6,
  output D_7
);

  Demultiplexer #(.select(2)) demultiplexer_1 (
    .out0(D_0), .out1(D_1_2), .out2(D_2_2), .out3(D_3_2), .in(in_1), .sel({S_1, S_0}));  // open: en
  Demultiplexer #(.select(3)) demultiplexer_2 (
    .out0(D_0_2), .out1(D_1), .out2(D_2), .out3(D_3), .out4(D_4), .out5(D_5), .out6(D_6), .out7(D_7),
    .in(in_2), .sel({S_2, S_1_2, S_0_2}));  // open: en

  // Notes on the sheet:
  //   Abstracted 1x4 DMX
  //   Abstracted 1x8 DMX
endmodule

module _16x8Demultiplexer (
  input  [15:0] I,
  input  S_2,
  input  S_1,
  input  S_0,
  output [15:0] D_0,
  output [15:0] D_1,
  output [15:0] D_2,
  output [15:0] D_3,
  output [15:0] D_4,
  output [15:0] D_5,
  output [15:0] D_6,
  output [15:0] D_7
);

  Demultiplexer #(.select(3), .width(16)) demultiplexer_1 (
    .out0(D_0), .out1(D_1), .out2(D_2), .out3(D_3), .out4(D_4), .out5(D_5), .out6(D_6), .out7(D_7), .in(I),
    .sel({S_2, S_1, S_0}));  // open: en

  // Notes on the sheet:
  //   Abstracted 8x16 DMX with Buses
endmodule

module MUXtoDMX (
  input  [15:0] I_0,
  input  [15:0] I_1,
  input  [15:0] I_2,
  input  [15:0] I_3,
  input  [15:0] I_4,
  input  [15:0] I_5,
  input  [15:0] I_6,
  input  ENABLE,
  input  S_2,
  input  S_1,
  input  S_0,
  input  [15:0] I_7,
  output [15:0] D_0,
  output [15:0] D_1,
  output [15:0] D_2,
  output [15:0] D_3,
  output [15:0] D_4,
  output [15:0] D_5,
  output [15:0] D_6,
  output [15:0] D_7
);

  wire [15:0] multiplexer_1_out;

  Multiplexer #(.select(3), .width(16), .enable("true")) multiplexer_1 (
    .in0(I_0), .in1(I_1), .in2(I_2), .in3(I_3), .in4(I_4), .in5(I_5), .in6(I_6), .in7(I_7),
    .out(multiplexer_1_out), .sel({S_2, S_1, S_0}), .en(ENABLE));
  Demultiplexer #(.select(3), .width(16), .enable("true")) demultiplexer_1 (
    .out0(D_0), .out1(D_1), .out2(D_2), .out3(D_3), .out4(D_4), .out5(D_5), .out6(D_6), .out7(D_7),
    .in(multiplexer_1_out), .sel({S_2, S_1, S_0}), .en(ENABLE));

  // Notes on the sheet:
  //   INPUT BUSES
  //   SELECT
  //   OUTPUT BUSES
endmodule
